// Logisim project control-logic.circ as structural Verilog: 1 circuit, main circuit control_logic
module control_logic (
  input  [31:0] Instruction,
  input  BrEq,
  input  BrLt,
  output PCSel,
  output RegWEn,
  output [2:0] ImmSel,
  output BrUn,
  output ASel,
  output BSel,
  output [3:0] ALUSel,
  output MemWEn,
  output [1:0] WBSel
);

  wire add_inst, addi_inst, and_2_out, and_3_out, and_15_out, and_16_out, and_17_out, and_18_out, and_inst,
       andi_inst, auipc_inst, b_type_inst, beq_inst, bge_inst, bgeu_inst, blt_inst, bltu_inst, bne_inst,
       comparator_9_eq, comparator_10_eq, comparator_11_eq, comparator_12_eq, comparator_13_eq,
       comparator_14_eq, comparator_15_eq, comparator_16_eq, comparator_17_eq, comparator_18_eq,
       comparator_19_eq, comparator_20_eq, comparator_21_eq, comparator_22_eq, comparator_23_eq,
       comparator_24_eq, comparator_25_eq, comparator_26_eq, comparator_27_eq, comparator_28_eq,
       comparator_29_eq, comparator_30_eq, comparator_31_eq, comparator_32_eq, comparator_33_eq,
       comparator_34_eq, comparator_35_eq, comparator_36_eq, comparator_37_eq, comparator_38_eq,
       comparator_39_eq, comparator_40_eq, comparator_41_eq, comparator_42_eq, comparator_43_eq,
       comparator_44_eq, comparator_45_eq, comparator_46_eq, comparator_47_eq, comparator_48_eq,
       comparator_49_eq, comparator_50_eq, comparator_51_eq, comparator_52_eq, comparator_53_eq,
       comparator_54_eq, comparator_55_eq, comparator_56_eq, comparator_57_eq, i_type_inst, i_type_inst_load,
       jal_inst, jalr_inst, lb_inst, lh_inst, lui_inst, lw_inst, mul_inst, mulh_inst, mulhu_inst, not_1_out,
       not_2_out, not_3_out, or_inst, ori_inst, r_type_inst, s_type_inst, sb_inst, sh_inst, sll_inst,
       slli_inst, slt_inst, slti_inst, sra_inst, srai_inst, srl_inst, srli_inst, sub_inst, sw_inst, xor_inst,
       xori_inst;
  wire [5:0] rom_input;
  wire [15:14] rom_1_data;

  Comparator #(.width(7)) comparator_1 (.a(Instruction[6:0]), .b(7'b0010011), .eq(i_type_inst));  // open: gt, lt
  Comparator #(.width(7)) comparator_2 (.a(Instruction[6:0]), .b(7'b0110011), .eq(r_type_inst));  // open: gt, lt
  Comparator #(.width(7)) comparator_3 (.a(Instruction[6:0]), .b(7'b1100011), .eq(b_type_inst));  // open: gt, lt
  Comparator #(.width(7)) comparator_4 (.a(Instruction[6:0]), .b(7'b0100011), .eq(s_type_inst));  // open: gt, lt
  Comparator #(.width(7)) comparator_5 (.a(Instruction[6:0]), .b(7'b0000011), .eq(i_type_inst_load));  // open: gt, lt
  Comparator #(.width(7)) comparator_6 (.a(Instruction[6:0]), .b(7'b1101111), .eq(jal_inst));  // open: gt, lt
  Comparator #(.width(7)) comparator_7 (.a(Instruction[6:0]), .b(7'b0010111), .eq(auipc_inst));  // open: gt, lt
  Comparator #(.width(7)) comparator_8 (.a(Instruction[6:0]), .b(7'b0110111), .eq(lui_inst));  // open: gt, lt
  Comparator #(.width(7)) comparator_9 (.a(Instruction[6:0]), .b(7'b1100111), .eq(comparator_9_eq));  // open: gt, lt
  Comparator #(.width(3)) comparator_10 (.a(Instruction[14:12]), .b(3'b000), .eq(comparator_10_eq));  // open: gt, lt
  ROM #(.addrWidth(6), .dataWidth(16)) rom_1 (
    .addr(rom_input), .data({rom_1_data, WBSel, MemWEn, ALUSel, BSel, ASel, BrUn, ImmSel, RegWEn}));
  and and_1 (jalr_inst, comparator_9_eq, comparator_10_eq);
  Comparator #(.width(7)) comparator_11 (.a(Instruction[31:25]), .b({7{1'b0}}), .eq(comparator_11_eq));  // open: gt, lt
  Comparator #(.width(7)) comparator_12 (.a(Instruction[31:25]), .b({7{1'b0}}), .eq(comparator_12_eq));  // open: gt, lt
  Comparator #(.width(7)) comparator_13 (
    .a(Instruction[31:25]), .b(7'b0100000), .eq(comparator_13_eq));  // open: gt, lt
  Comparator #(.width(3)) comparator_14 (.a(Instruction[14:12]), .b(3'b000), .eq(comparator_14_eq));  // open: gt, lt
  Comparator #(.width(3)) comparator_15 (.a(Instruction[14:12]), .b(3'b111), .eq(comparator_15_eq));  // open: gt, lt
  Comparator #(.width(3)) comparator_16 (.a(Instruction[14:12]), .b(3'b110), .eq(comparator_16_eq));  // open: gt, lt
  Comparator #(.width(3)) comparator_17 (.a(Instruction[14:12]), .b(3'b100), .eq(comparator_17_eq));  // open: gt, lt
  Comparator #(.width(3)) comparator_18 (.a(Instruction[14:12]), .b(3'b010), .eq(comparator_18_eq));  // open: gt, lt
  Comparator #(.width(3)) comparator_19 (.a(Instruction[14:12]), .b(3'b001), .eq(comparator_19_eq));  // open: gt, lt
  Comparator #(.width(3)) comparator_20 (.a(Instruction[14:12]), .b(3'b101), .eq(comparator_20_eq));  // open: gt, lt
  Comparator #(.width(3)) comparator_21 (.a(Instruction[14:12]), .b(3'b101), .eq(comparator_21_eq));  // open: gt, lt
  Comparator #(.width(3)) comparator_22 (.a(Instruction[14:12]), .b(3'b000), .eq(comparator_22_eq));  // open: gt, lt
  Comparator #(.width(3)) comparator_23 (.a(Instruction[14:12]), .b(3'b001), .eq(comparator_23_eq));  // open: gt, lt
  Comparator #(.width(3)) comparator_24 (.a(Instruction[14:12]), .b(3'b010), .eq(comparator_24_eq));  // open: gt, lt
  and and_2 (and_2_out, blt_inst, BrLt);
  and and_3 (and_3_out, bltu_inst, BrLt);
  and and_4 (addi_inst, i_type_inst, comparator_14_eq);
  and and_5 (andi_inst, i_type_inst, comparator_15_eq);
  and and_6 (ori_inst, i_type_inst, comparator_16_eq);
  and and_7 (xori_inst, i_type_inst, comparator_17_eq);
  and and_8 (slti_inst, i_type_inst, comparator_18_eq);
  and and_9 (slli_inst, i_type_inst, comparator_11_eq, comparator_19_eq);
  and and_10 (srli_inst, i_type_inst, comparator_12_eq, comparator_20_eq);
  and and_11 (srai_inst, i_type_inst, comparator_13_eq, comparator_21_eq);
  and and_12 (lb_inst, i_type_inst_load, comparator_22_eq);
  and and_13 (lh_inst, i_type_inst_load, comparator_23_eq);
  and and_14 (lw_inst, i_type_inst_load, comparator_24_eq);
  and and_15 (and_15_out, beq_inst, BrEq);
  and and_16 (and_16_out, bne_inst, not_1_out);
  not not_1 (not_1_out, BrEq);
  not not_2 (not_2_out, BrLt);
  and and_17 (and_17_out, not_2_out, bge_inst);
  not not_3 (not_3_out, BrLt);
  and and_18 (and_18_out, not_3_out, bgeu_inst);
  Comparator #(.width(3)) comparator_25 (.a(Instruction[14:12]), .b(3'b000), .eq(comparator_25_eq));  // open: gt, lt
  Comparator #(.width(3)) comparator_26 (.a(Instruction[14:12]), .b(3'b001), .eq(comparator_26_eq));  // open: gt, lt
  Comparator #(.width(3)) comparator_27 (.a(Instruction[14:12]), .b(3'b010), .eq(comparator_27_eq));  // open: gt, lt
  or or_1 (PCSel, jal_inst, jalr_inst, and_15_out, and_17_out, and_16_out, and_18_out, and_2_out, and_3_out);
  Comparator #(.width(7)) comparator_28 (.a(Instruction[31:25]), .b({7{1'b0}}), .eq(comparator_28_eq));  // open: gt, lt
  Comparator #(.width(7)) comparator_29 (
    .a(Instruction[31:25]), .b(7'b0100000), .eq(comparator_29_eq));  // open: gt, lt
  Comparator #(.width(7)) comparator_30 (.a(Instruction[31:25]), .b({7{1'b0}}), .eq(comparator_30_eq));  // open: gt, lt
  Comparator #(.width(7)) comparator_31 (.a(Instruction[31:25]), .b({7{1'b0}}), .eq(comparator_31_eq));  // open: gt, lt
  Comparator #(.width(7)) comparator_32 (.a(Instruction[31:25]), .b({7{1'b0}}), .eq(comparator_32_eq));  // open: gt, lt
  Comparator #(.width(7)) comparator_33 (.a(Instruction[31:25]), .b({7{1'b0}}), .eq(comparator_33_eq));  // open: gt, lt
  Comparator #(.width(3)) comparator_34 (.a(Instruction[14:12]), .b(3'b000), .eq(comparator_34_eq));  // open: gt, lt
  Comparator #(.width(3)) comparator_35 (.a(Instruction[14:12]), .b(3'b000), .eq(comparator_35_eq));  // open: gt, lt
  Comparator #(.width(3)) comparator_36 (.a(Instruction[14:12]), .b(3'b111), .eq(comparator_36_eq));  // open: gt, lt
  Comparator #(.width(3)) comparator_37 (.a(Instruction[14:12]), .b(3'b110), .eq(comparator_37_eq));  // open: gt, lt
  Comparator #(.width(3)) comparator_38 (.a(Instruction[14:12]), .b(3'b100), .eq(comparator_38_eq));  // open: gt, lt
  Comparator #(.width(3)) comparator_39 (.a(Instruction[14:12]), .b(3'b001), .eq(comparator_39_eq));  // open: gt, lt
  and and_19 (sb_inst, s_type_inst, comparator_25_eq);
  and and_20 (sh_inst, s_type_inst, comparator_26_eq);
  and and_21 (sw_inst, s_type_inst, comparator_27_eq);
  and and_22 (add_inst, r_type_inst, comparator_28_eq, comparator_34_eq);
  and and_23 (sub_inst, r_type_inst, comparator_29_eq, comparator_35_eq);
  and and_24 (and_inst, r_type_inst, comparator_30_eq, comparator_36_eq);
  and and_25 (or_inst, r_type_inst, comparator_31_eq, comparator_37_eq);
  and and_26 (xor_inst, r_type_inst, comparator_32_eq, comparator_38_eq);
  and and_27 (sll_inst, r_type_inst, comparator_33_eq, comparator_39_eq);
  Comparator #(.width(7)) comparator_40 (.a(Instruction[31:25]), .b({7{1'b0}}), .eq(comparator_40_eq));  // open: gt, lt
  Comparator #(.width(7)) comparator_41 (
    .a(Instruction[31:25]), .b(7'b0100000), .eq(comparator_41_eq));  // open: gt, lt
  Comparator #(.width(7)) comparator_42 (.a(Instruction[31:25]), .b({7{1'b0}}), .eq(comparator_42_eq));  // open: gt, lt
  Comparator #(.width(7)) comparator_43 (
    .a(Instruction[31:25]), .b(7'b0000001), .eq(comparator_43_eq));  // open: gt, lt
  Comparator #(.width(7)) comparator_44 (
    .a(Instruction[31:25]), .b(7'b0000001), .eq(comparator_44_eq));  // open: gt, lt
  Comparator #(.width(7)) comparator_45 (
    .a(Instruction[31:25]), .b(7'b0000001), .eq(comparator_45_eq));  // open: gt, lt
  Comparator #(.width(3)) comparator_46 (.a(Instruction[14:12]), .b(3'b101), .eq(comparator_46_eq));  // open: gt, lt
  Comparator #(.width(3)) comparator_47 (.a(Instruction[14:12]), .b(3'b101), .eq(comparator_47_eq));  // open: gt, lt
  Comparator #(.width(3)) comparator_48 (.a(Instruction[14:12]), .b(3'b010), .eq(comparator_48_eq));  // open: gt, lt
  Comparator #(.width(3)) comparator_49 (.a(Instruction[14:12]), .b(3'b000), .eq(comparator_49_eq));  // open: gt, lt
  Comparator #(.width(3)) comparator_50 (.a(Instruction[14:12]), .b(3'b001), .eq(comparator_50_eq));  // open: gt, lt
  Comparator #(.width(3)) comparator_51 (.a(Instruction[14:12]), .b(3'b011), .eq(comparator_51_eq));  // open: gt, lt
  and and_28 (srl_inst, r_type_inst, comparator_40_eq, comparator_46_eq);
  and and_29 (sra_inst, r_type_inst, comparator_41_eq, comparator_47_eq);
  and and_30 (slt_inst, r_type_inst, comparator_42_eq, comparator_48_eq);
  and and_31 (mul_inst, r_type_inst, comparator_43_eq, comparator_49_eq);
  and and_32 (mulh_inst, r_type_inst, comparator_44_eq, comparator_50_eq);
  and and_33 (mulhu_inst, r_type_inst, comparator_45_eq, comparator_51_eq);
  Priority_Encoder #(.select_enc(6)) priority_encoder_1 (
    .in0(add_inst), .in1(mul_inst), .in2(sub_inst), .in3(sll_inst), .in4(mulh_inst), .in5(mulhu_inst),
    .in6(slt_inst), .in7(xor_inst), .in8(srl_inst), .in9(sra_inst), .in10(or_inst), .in11(and_inst),
    .in12(lb_inst), .in13(lh_inst), .in14(lw_inst), .in15(addi_inst), .in16(slli_inst), .in17(slti_inst),
    .in18(xori_inst), .in19(srli_inst), .in20(srai_inst), .in21(ori_inst), .in22(andi_inst), .in23(sb_inst),
    .in24(sh_inst), .in25(sw_inst), .in26(beq_inst), .in27(bne_inst), .in28(blt_inst), .in29(bge_inst),
    .in30(bltu_inst), .in31(bgeu_inst), .in32(auipc_inst), .in33(lui_inst), .in34(jal_inst),
    .in35(jalr_inst), .out(rom_input));  // open: in36, in37, in38, in39, in40, in41, in42, in43, in44, in45, in46, in47, in48, in49, in50, in51, in52, in53, in54, in55, in56, in57, in58, in59, in60, in61, in62, in63, gs, en_out, en_in
  Comparator #(.width(3)) comparator_52 (.a(Instruction[14:12]), .b(3'b000), .eq(comparator_52_eq));  // open: gt, lt
  Comparator #(.width(3)) comparator_53 (.a(Instruction[14:12]), .b(3'b101), .eq(comparator_53_eq));  // open: gt, lt
  Comparator #(.width(3)) comparator_54 (.a(Instruction[14:12]), .b(3'b111), .eq(comparator_54_eq));  // open: gt, lt
  Comparator #(.width(3)) comparator_55 (.a(Instruction[14:12]), .b(3'b100), .eq(comparator_55_eq));  // open: gt, lt
  Comparator #(.width(3)) comparator_56 (.a(Instruction[14:12]), .b(3'b110), .eq(comparator_56_eq));  // open: gt, lt
  Comparator #(.width(3)) comparator_57 (.a(Instruction[14:12]), .b(3'b001), .eq(comparator_57_eq));  // open: gt, lt
  and and_34 (beq_inst, b_type_inst, comparator_52_eq);
  and and_35 (bge_inst, b_type_inst, comparator_53_eq);
  and and_36 (bgeu_inst, b_type_inst, comparator_54_eq);
  and and_37 (blt_inst, b_type_inst, comparator_55_eq);
  and and_38 (bltu_inst, b_type_inst, comparator_56_eq);
  and and_39 (bne_inst, b_type_inst, comparator_57_eq);

  // Other names for the same wires on the sheet: opcode[6:0] = Instruction[6:0]; funct3[2:0] = Instruction[14:12];
  //   funct7[6:0] = Instruction[31:25]

  // Notes on the sheet:
  //   INPUTS to your circuit
  //   Connect ROM Input here ->
  //   contents of rom_1 (hex, n*v repeats v):
  //   101f 141f 161f 109f 149f 159f 111f 121f 129f 169f 131f 139f 41 41 41 1051 10d1 1151 1251 12d1 16d1
  //   1351 13d1 1852 1852 1852 3074 3074 3064 3064 3074 3074 1077 17f7 2079 2051
  //   ROM FOR CONTROL LOGIC
  //   DON'T CHANGE THE LOCATIONS OF THE INPUTS AND OUTPUTS!
  //   This is only if you choose to do the ROM option
  //   CONNECT
  //   WIRE
  //   TO
  //   USE
  //   ROM
  //   OUTPUT from your circuit
  //   Reminder: If using ROM, use combinational logic for PCSel
endmodule
