// Logisim project cpu.circ as structural Verilog: 1 circuit, main circuit cpu
module cpu (
  input  clk,
  input  [31:0] Instruction,
  input  [31:0] MemReadData,
  output [31:0] MemAddress,
  output [31:0] ProgramCounter,
  output [31:0] ra,
  output [31:0] sp,
  output [31:0] t0,
  output [31:0] t1,
  output [31:0] t2,
  output [31:0] s0,
  output [31:0] s1,
  output [31:0] a0,
  output [3:0] MemWriteMask,
  output [31:0] MemWriteData
);

  wire ASel, BrEq, BrLt, BrUn, BSel, comparator_1_eq, MemWEn, NewPCSel, PCSel, RegWEn;
  wire [1:0] WBSel;
  wire [2:0] ImmSel;
  wire [3:0] ALUSel;
  wire [31:0] DataFromReg, imm_gen_1_immediate, Instruction2, MemDataToReg, multiplexer_1_out,
       multiplexer_2_out, multiplexer_3_out, multiplexer_4_out, pc_plus_4, pc_plus_4_s2, regfile_1_readdata1,
       register_2_q, WD;

  Adder #(.width(32)) adder_1 (.a(ProgramCounter), .b(32'h4), .out(pc_plus_4));  // open: cin, cout
  Multiplexer #(.width(32)) multiplexer_1 (.in0(pc_plus_4), .in1(MemAddress), .out(multiplexer_1_out), .sel(PCSel));
  Register #(.width(32)) PC (.D(multiplexer_1_out), .clk(clk), .Q(ProgramCounter));  // open: en, clr
  Multiplexer #(.width(32)) multiplexer_2 (.in0(Instruction), .in1(32'h13), .out(multiplexer_2_out), .sel(PCSel));
  Register #(.width(32)) register_1 (.D(multiplexer_2_out), .clk(clk), .Q(Instruction2));  // open: en, clr
  Comparator #(.width(32)) comparator_1 (.a(Instruction), .b({32{1'b0}}), .eq(comparator_1_eq));  // open: gt, lt
  or or_1 (NewPCSel, PCSel, comparator_1_eq);
  control_logic control_logic_1 (
    .PCSel(PCSel), .RegWEn(RegWEn), .ImmSel(ImmSel), .BrUn(BrUn), .ASel(ASel), .BSel(BSel), .ALUSel(ALUSel),
    .MemWEn(MemWEn), .WBSel(WBSel), .Instruction(Instruction2), .BrEq(BrEq), .BrLt(BrLt));
  regfile regfile_1 (
    .ReadIndex1(Instruction2[19:15]), .ReadIndex2(Instruction2[24:20]), .WriteIndex(Instruction2[11:7]),
    .WriteData(WD), .RegWEn(RegWEn), .clk(clk), .ra(ra), .sp(sp), .t0(t0), .t1(t1), .t2(t2), .s0(s0),
    .s1(s1), .a0(a0), .ReadData1(regfile_1_readdata1), .ReadData2(DataFromReg));
  imm_gen imm_gen_1 (.Instruction(Instruction2), .ImmSel(ImmSel), .Immediate(imm_gen_1_immediate));
  Multiplexer #(.width(32)) multiplexer_3 (
    .in0(regfile_1_readdata1), .in1(register_2_q), .out(multiplexer_3_out), .sel(ASel));
  Multiplexer #(.width(32)) multiplexer_4 (
    .in0(DataFromReg), .in1(imm_gen_1_immediate), .out(multiplexer_4_out), .sel(BSel));
  alu alu_1 (.ALUResult(MemAddress), .A(multiplexer_3_out), .B(multiplexer_4_out), .ALUSel(ALUSel));
  Register #(.width(32)) register_2 (.D(ProgramCounter), .clk(clk), .Q(register_2_q));  // open: en, clr
  branch_comp branch_comp_1 (
    .BrData1(regfile_1_readdata1), .BrData2(DataFromReg), .BrUn(BrUn), .BrEq(BrEq), .BrLt(BrLt));
  Adder #(.width(32)) adder_2 (.a(register_2_q), .b(32'h4), .out(pc_plus_4_s2));  // open: cin, cout
  Multiplexer #(.select(2), .width(32)) multiplexer_5 (
    .in0(MemDataToReg), .in1(MemAddress), .in2(pc_plus_4_s2), .out(WD), .sel(WBSel));  // open: in3
  partial_store partial_store_1 (
    .Instruction(Instruction2), .MemAddress(MemAddress), .DataFromReg(DataFromReg), .MemWEn(MemWEn),
    .MemWriteMask(MemWriteMask), .DataToMem(MemWriteData));
  partial_load partial_load_1 (
    .Instruction(Instruction2), .MemAddress(MemAddress), .DataFromMem(MemReadData), .DataToReg(MemDataToReg));

  // Notes on the sheet:
  //   To IMEM
  //   IMEM (do **NOT** move this)
  //   From IMEM
  //   Inputs/Outputs for testing. Do **NOT** move these.
  //   To DMEM
  //   DMEM (do **NOT** move this)
  //   From DMEM
endmodule
