// Logisim project regfile.circ as structural Verilog: 1 circuit, main circuit regfile
module regfile (
  input  [4:0] ReadIndex1,
  input  [4:0] ReadIndex2,
  input  [4:0] WriteIndex,
  input  [31:0] WriteData,
  input  RegWEn,
  input  clk,
  output [31:0] ra,
  output [31:0] sp,
  output [31:0] t0,
  output [31:0] t1,
  output [31:0] t2,
  output [31:0] s0,
  output [31:0] s1,
  output [31:0] a0,
  output [31:0] ReadData1,
  output [31:0] ReadData2
);

  wire a0WE, a1WE, a2WE, a3WE, a4WE, a5WE, a6WE, a7WE, gpWE, raWE, s0WE, s1WE, s2WE, s3WE, s4WE, s5WE, s6WE,
       s7WE, s8WE, s9WE, s10WE, s11WE, spWE, t0WE, t1WE, t2WE, t3WE, t4WE, t5WE, t6WE, tpWE;
  wire [31:0] a1, a2, a3, a4, a5, a6, a7, gp, s2, s3, s4, s5, s6, s7, s8, s9, s10, s11, t3, t4, t5, t6, tp;

  Demultiplexer #(.select(5)) demultiplexer_1 (
    .out1(raWE), .out2(spWE), .out3(gpWE), .out4(tpWE), .out5(t0WE), .out6(t1WE), .out7(t2WE), .out8(s0WE),
    .out9(s1WE), .out10(a0WE), .out11(a1WE), .out12(a2WE), .out13(a3WE), .out14(a4WE), .out15(a5WE),
    .out16(a6WE), .out17(a7WE), .out18(s2WE), .out19(s3WE), .out20(s4WE), .out21(s5WE), .out22(s6WE),
    .out23(s7WE), .out24(s8WE), .out25(s9WE), .out26(s10WE), .out27(s11WE), .out28(t3WE), .out29(t4WE),
    .out30(t5WE), .out31(t6WE), .in(RegWEn), .sel(WriteIndex));  // open: out0
  Register #(.width(32)) raREG (.D(WriteData), .en(raWE), .clk(clk), .Q(ra));  // open: clr
  Register #(.width(32)) spREG (.D(WriteData), .en(spWE), .clk(clk), .Q(sp));  // open: clr
  Register #(.width(32)) s8REG (.D(WriteData), .en(s8WE), .clk(clk), .Q(s8));  // open: clr
  Register #(.width(32)) s9REG (.D(WriteData), .en(s9WE), .clk(clk), .Q(s9));  // open: clr
  Register #(.width(32)) s10REG (.D(WriteData), .en(s10WE), .clk(clk), .Q(s10));  // open: clr
  Register #(.width(32)) s11REG (.D(WriteData), .en(s11WE), .clk(clk), .Q(s11));  // open: clr
  Register #(.width(32)) t3REG (.D(WriteData), .en(t3WE), .clk(clk), .Q(t3));  // open: clr
  Register #(.width(32)) t4REG (.D(WriteData), .en(t4WE), .clk(clk), .Q(t4));  // open: clr
  Register #(.width(32)) t0REG (.D(WriteData), .en(t0WE), .clk(clk), .Q(t0));  // open: clr
  Register #(.width(32)) t1REG (.D(WriteData), .en(t1WE), .clk(clk), .Q(t1));  // open: clr
  Register #(.width(32)) t5REG (.D(WriteData), .en(t5WE), .clk(clk), .Q(t5));  // open: clr
  Register #(.width(32)) t6REG (.D(WriteData), .en(t6WE), .clk(clk), .Q(t6));  // open: clr
  Register #(.width(32)) t2REG (.D(WriteData), .en(t2WE), .clk(clk), .Q(t2));  // open: clr
  Register #(.width(32)) s0REG (.D(WriteData), .en(s0WE), .clk(clk), .Q(s0));  // open: clr
  Register #(.width(32)) s2REG (.D(WriteData), .en(s2WE), .clk(clk), .Q(s2));  // open: clr
  Register #(.width(32)) s3REG (.D(WriteData), .en(s3WE), .clk(clk), .Q(s3));  // open: clr
  Register #(.width(32)) s4REG (.D(WriteData), .en(s4WE), .clk(clk), .Q(s4));  // open: clr
  Register #(.width(32)) s5REG (.D(WriteData), .en(s5WE), .clk(clk), .Q(s5));  // open: clr
  Register #(.width(32)) s6REG (.D(WriteData), .en(s6WE), .clk(clk), .Q(s6));  // open: clr
  Register #(.width(32)) s7REG (.D(WriteData), .en(s7WE), .clk(clk), .Q(s7));  // open: clr
  Register #(.width(32)) s1REG (.D(WriteData), .en(s1WE), .clk(clk), .Q(s1));  // open: clr
  Register #(.width(32)) gpREG (.D(WriteData), .en(gpWE), .clk(clk), .Q(gp));  // open: clr
  Register #(.width(32)) tpREG (.D(WriteData), .en(tpWE), .clk(clk), .Q(tp));  // open: clr
  Register #(.width(32)) a0REG (.D(WriteData), .en(a0WE), .clk(clk), .Q(a0));  // open: clr
  Register #(.width(32)) a1REG (.D(WriteData), .en(a1WE), .clk(clk), .Q(a1));  // open: clr
  Register #(.width(32)) a2REG (.D(WriteData), .en(a2WE), .clk(clk), .Q(a2));  // open: clr
  Register #(.width(32)) a3REG (.D(WriteData), .en(a3WE), .clk(clk), .Q(a3));  // open: clr
  Register #(.width(32)) a4REG (.D(WriteData), .en(a4WE), .clk(clk), .Q(a4));  // open: clr
  Register #(.width(32)) a5REG (.D(WriteData), .en(a5WE), .clk(clk), .Q(a5));  // open: clr
  Register #(.width(32)) a6REG (.D(WriteData), .en(a6WE), .clk(clk), .Q(a6));  // open: clr
  Register #(.width(32)) a7REG (.D(WriteData), .en(a7WE), .clk(clk), .Q(a7));  // open: clr
  Multiplexer #(.select(5), .width(32)) multiplexer_1 (
    .in0({32{1'b0}}), .in1(ra), .in2(sp), .in3(gp), .in4(tp), .in5(t0), .in6(t1), .in7(t2), .in8(s0),
    .in9(s1), .in10(a0), .in11(a1), .in12(a2), .in13(a3), .in14(a4), .in15(a5), .in16(a6), .in17(a7),
    .in18(s2), .in19(s3), .in20(s4), .in21(s5), .in22(s6), .in23(s7), .in24(s8), .in25(s9), .in26(s10),
    .in27(s11), .in28(t3), .in29(t4), .in30(t5), .in31(t6), .out(ReadData1), .sel(ReadIndex1));
  Multiplexer #(.select(5), .width(32)) multiplexer_2 (
    .in0({32{1'b0}}), .in1(ra), .in2(sp), .in3(gp), .in4(tp), .in5(t0), .in6(t1), .in7(t2), .in8(s0),
    .in9(s1), .in10(a0), .in11(a1), .in12(a2), .in13(a3), .in14(a4), .in15(a5), .in16(a6), .in17(a7),
    .in18(s2), .in19(s3), .in20(s4), .in21(s5), .in22(s6), .in23(s7), .in24(s8), .in25(s9), .in26(s10),
    .in27(s11), .in28(t3), .in29(t4), .in30(t5), .in31(t6), .out(ReadData2), .sel(ReadIndex2));

  // Notes on the sheet:
  //   INPUTS to your circuit
  //   DON'T CHANGE THE LOCATIONS OF THE INPUTS AND OUTPUTS!
  //   These are DEBUG/TEST outputs from your circuit.
  //   OUTPUTS from your circuit
endmodule
